# Fritzing sketch digitalDisplay_Sketch (saved by Fritzing 0.9.3b)
breadboards: 1

parts:
  R1 = Resistor [tolerance=±1% resistance=1k package=THT]
  R2 = Resistor [tolerance=±1% resistance=1k package=THT]
  R3 = Resistor [tolerance=±1% resistance=1k package=THT]
  R5 = Resistor [tolerance=±1% resistance=1k package=THT]
  R6 = Resistor [tolerance=±1% resistance=1k package=THT]
  R7 = Resistor [tolerance=±1% resistance=1k package=THT]
  R8 = Resistor [tolerance=±1% resistance=1k package=THT]
  R9 = Resistor [tolerance=±1% resistance=1k package=THT]
  7_Segment1 = 7 Segment Display
  Raspberry_Pi_1 = Raspberry Pi 3 [part_number=RPI-3-V1.2]
  S1 = Pushbutton [package="[THT]"]
  R10 = Resistor [tolerance=±5% resistance=10k package=THT]
  C2 = Ceramic Capacitor [capacitance=0.1µF voltage=50V package="200 mil [THT, multilayer]"]

nets:
  N1: R1.Pin_0, Raspberry_Pi_1.GPIO16
  N2: R1.Pin_1, 7_Segment1.Segment_D
  N3: R2.Pin_0, 7_Segment1.Segment_C
  N4: R2.Pin_1, Raspberry_Pi_1.GPIO24
  N5: R3.Pin_0, 7_Segment1.Segment_DP
  N6: R3.Pin_1, Raspberry_Pi_1.GPIO23
  N7: R5.Pin_0, Raspberry_Pi_1.GPIO20
  N8: R5.Pin_1, 7_Segment1.Segment_E
  N9: R6.Pin_0, Raspberry_Pi_1.GPIO19
  N10: R6.Pin_1, 7_Segment1.Segment_F
  N11: R7.Pin_0, 7_Segment1.Segment_B
  N12: R7.Pin_1, Raspberry_Pi_1.GPIO5
  N13: R8.Pin_0, Raspberry_Pi_1.GPIO26
  N14: R8.Pin_1, 7_Segment1.Segment_G
  N15: R9.Pin_0, 7_Segment1.Segment_A
  N16: R9.Pin_1, Raspberry_Pi_1.GPIO6
  N17: 7_Segment1.common_cathode, Raspberry_Pi_1.GND, S1.Pin_1, S1.Pin_2, C2.1
  N18: Raspberry_Pi_1.1#_3v3, R10.Pin_0
  N19: Raspberry_Pi_1.GPIO21, S1.Pin_3, S1.Pin_4, R10.Pin_1, C2.0

notes:
  Sysolve IoT 开源项目
  Android Things 数码管显示
  购买所需元件？请访问sysolve.taobao.com
  本案例适用于
  树莓派 Raspberry Pi 3B
  NXP Pico i.MX7D 开发板
  NXP Pico i.MX6UL 开发板

custom parts:
  Raspberry Pi 3: The RPi3, a faster version of the awesome Raspberry Pi 2 B ARM Board with 40 pin gpio. Ready for special Raspberry Pi B+ and RPi2 Hat (Hardware attached (on) top)
